# Fritzing sketch Untitled Sketch (saved by Fritzing 0.9.3b)
breadboards: 1

parts:
  U1 = NodeMCU V3.0
  DHT1 = DHT22 Humidity and Temperature Sensor

nets:
  N1: U1.D4, DHT1.DATA
  3V3: U1.3V3, DHT1.VDD
  N2: U1.GND#6, U1.GND#13, U1.GND#16, U1.GND#33, DHT1.GND

custom parts:
  NodeMCU V3.0: ESP8266 based NodeMCU
